// Digital circuit 555-timer-driving-digital-counter-analog-oscillator-to-digital-count.dig as structural Verilog
module _555_timer_driving_digital_counter_analog_oscillator_to_digital_count (
  output [3:0] Q
);

  wire Ra_p1, T555_p1;

  // DcVoltageSource Vcc: pin names not known; wires that end beside it: 1'b0
  // Resistor Ra: pin names not known; wires that end beside it: Ra_p1, 1'b1, 1'b1
  // Timer555 T555: pin names not known; wires that end beside it: T555_p1, Ra_p1, Q
  // Resistor Rb: pin names not known; wires that end beside it: T555_p1, Ra_p1
  // Capacitor C1: pin names not known; wires that end beside it: 1'b0, 1'b0
  Counter #(.simulationModel("digital")) CNT ();  // open: en, C, clr, out, ovf
endmodule
