// Digital circuit adc-readout-analog-waveform-sampled-to-digital-outputs.dig as structural Verilog
module adc_readout_analog_waveform_sampled_to_digital_outputs (
  input  CLK,
  output Q0,
  output Q1,
  output Q2,
  output Q3
);

  // AcVoltageSource Vs: pin names not known; wires that end beside it: 1'b0
  // Resistor R1: pin names not known; wires that end beside it: CLK
  // DcVoltageSource Vref: pin names not known; wires that end beside it: 1'b0, 1'b0, Q3
  // ADC #(.Bits(4)) ADC1: pin names not known; wires that end beside it: Q0, Q1, Q2
endmodule
