// Digital circuit comparator-to-logic-analog-threshold-drives-digital-gate.dig as structural Verilog
module comparator_to_logic_analog_threshold_drives_digital_gate (
);

  // DcVoltageSource dcvoltagesource_1: pin names not known
endmodule
