// Digital circuit dac-rc-filter-digital-input-produces-filtered-analog-voltage.dig as structural Verilog
module dac_rc_filter_digital_input_produces_filtered_analog_voltage (
  input  D0,
  input  D1,
  input  D2,
  input  D3
);

  wire DAC1_p4, Vref_p2;

  // DcVoltageSource Vref: pin names not known; wires that end beside it: 1'b0, Vref_p2, D0, D1, Vref_p2
  // DAC #(.Bits(4)) DAC1: pin names not known; wires that end beside it: D2, D3, 1'b0, DAC1_p4
  // Resistor R1: pin names not known; wires that end beside it: DAC1_p4
  // Capacitor C1: pin names not known; wires that end beside it: 1'b0
  // Probe P1 on 1'b0
endmodule
