// Digital circuit digital-controlled-analog-switch-in-toggles-analog-path.dig as structural Verilog
module digital_controlled_analog_switch_in_toggles_analog_path (
  input  CTRL
);

  // DcVoltageSource dcvoltagesource_1: pin names not known; wires that end beside it: CTRL
endmodule
