// Digital circuit digital-servo-loop-dac-to-opamp-to-adc-feedforward.dig as structural Verilog
module digital_servo_loop_dac_to_opamp_to_adc_feedforward (
);

  // DcVoltageSource Vref: pin names not known; wires that end beside it: 1'b1, 1'b0, 1'b0
endmodule
