// Digital circuit mixed-transistor-gate-bjt-level-shifts-into-digital-and.dig as structural Verilog
module mixed_transistor_gate_bjt_level_shifts_into_digital_and (
  output Y
);

  wire Rb_p1, Vcc_p2;

  // DcVoltageSource Vcc: pin names not known; wires that end beside it: 1'b0, Vcc_p2
  // Resistor Rb: pin names not known; wires that end beside it: Rb_p1
  // Resistor Rc: pin names not known; wires that end beside it: Vcc_p2, Rb_p1, 1'b1, 1'b1
  // NpnBJT Q1: pin names not known; wires that end beside it: 1'b0
  and G1d (Y, 1'b1, 1'b1);
endmodule
