// Digital circuit pwm-to-analog-voltage-counter-generated-pwm-filtered-to-dc.dig as structural Verilog
module pwm_to_analog_voltage_counter_generated_pwm_filtered_to_dc (
  input  CLK
);

  wire CMP_p3, CNT_out;

  Counter #(.simulationModel("digital")) CNT (.en(1'b1), .C(CLK), .out(CNT_out));  // open: clr, ovf
  // MagnitudeComparator #(.Bits(4)) CMP: pin names not known; wires that end beside it: CNT_out, 4'b1000, CMP_p3
  // Resistor R1: pin names not known; wires that end beside it: CMP_p3
  // Capacitor C1: pin names not known; wires that end beside it: 1'b0
  // Probe P1 on 1'b0
endmodule
