// Digital circuit register-file-write-and-read-registers.dig as structural Verilog
module register_file_write_and_read_registers (
);

  RegisterFile registerfile_1 ();  // open: Din, we, Rw, C, Ra, Rb, Da, Db
endmodule
