// Digital circuit relay-from-digital-logic-and-gate-drives-relay-coil.dig as structural Verilog
module relay_from_digital_logic_and_gate_drives_relay_coil (
  input  A,
  input  B
);

  // And G1 is placed but not wired
  // DcVoltageSource Vs: pin names not known; wires that end beside it: B, 1'b0
  // Relay #(.simulationModel("digital")) RLY: pin names not known; wires that end beside it: A
  // Resistor R1: pin names not known
endmodule
