// Digital circuit rom-lookup-read-preloaded-data-by-address.dig as structural Verilog
module rom_lookup_read_preloaded_data_by_address (
  input  A,
  output D
);

  ROM #(.AddrBits(2)) ROM ();  // open: A, sel, D
endmodule
