// Digital circuit t-flip-flop-4-bit-ripple-counter.dig as structural Verilog
module t_flip_flop_4_bit_ripple_counter (
  input  CLK,
  output Q0,
  output Q1,
  output Q2,
  output Q3
);

  T_FF #(.simulationModel("digital")) T1 (.T(1'b1), .C(CLK), .Q(Q0));  // open: nQ
  T_FF #(.simulationModel("digital")) T2 (.T(1'b1), .C(Q0), .Q(Q1));  // open: nQ
  T_FF #(.simulationModel("digital")) T3 (.T(1'b1), .C(Q1), .Q(Q2));  // open: nQ
  T_FF #(.simulationModel("digital")) T4 (.T(1'b1), .C(Q2), .Q(Q3));  // open: nQ
endmodule
