// Digital circuit dcswitchlrc.dig as structural Verilog
module dcswitchlrc (
);

  wire capacitor_1_p1, resistor_1_p2;

  // Capacitor #(.capacitance(0.0001)) capacitor_1: pin names not known; wires that end beside it: capacitor_1_p1, 1'b0
  // Resistor #(.resistance(100)) resistor_1: pin names not known; wires that end beside it: capacitor_1_p1, resistor_1_p2
  // Inductor #(.inductance(0.1)) inductor_1: pin names not known; wires that end beside it: resistor_1_p2, 1'b0
  // SwitchDT switchdt_1: pin names not known; wires that end beside it: resistor_1_p2
  // DcVoltageSource dcvoltagesource_1: pin names not known; wires that end beside it: 1'b0
endmodule
