// Digital circuit lrctest.dig as structural Verilog
module lrctest (
);

  wire capacitor_1_p1, capacitor_1_p2, resistor_1_p2;

  // Capacitor capacitor_1: pin names not known; wires that end beside it: capacitor_1_p1, capacitor_1_p2
  // Resistor resistor_1: pin names not known; wires that end beside it: capacitor_1_p1, resistor_1_p2
  // Inductor inductor_1: pin names not known; wires that end beside it: resistor_1_p2, capacitor_1_p2
  // AcVoltageSource acvoltagesource_1: pin names not known; wires that end beside it: capacitor_1_p2
endmodule
