// Digital circuit lrctestgnd.dig as structural Verilog
module lrctestgnd (
);

  wire capacitor_1_p1, resistor_1_p2;

  // Capacitor #(.capacitance(0.0001)) capacitor_1: pin names not known; wires that end beside it: capacitor_1_p1, 1'b0
  // Resistor resistor_1: pin names not known; wires that end beside it: capacitor_1_p1, resistor_1_p2
  // Inductor #(.inductance(0.1)) inductor_1: pin names not known; wires that end beside it: resistor_1_p2, 1'b0
  // AcVoltageSource acvoltagesource_1: pin names not known; wires that end beside it: 1'b0
endmodule
