// Digital circuit lrcxor.dig as structural Verilog
module lrcxor (
);

  wire capacitor_1_p1, resistor_1_p2, xor_1_out;

  // Capacitor #(.capacitance(0.0001)) capacitor_1: pin names not known; wires that end beside it: capacitor_1_p1, 1'b0
  // Resistor #(.resistance(100)) resistor_1: pin names not known; wires that end beside it: capacitor_1_p1, resistor_1_p2
  // Inductor #(.inductance(0.1)) inductor_1: pin names not known; wires that end beside it: resistor_1_p2, 1'b0
  // AcVoltageSource acvoltagesource_1: pin names not known; wires that end beside it: 1'b0
  xor xor_1 (xor_1_out, resistor_1_p2, 1'b0);
  // Resistor resistor_2: pin names not known; wires that end beside it: xor_1_out, 1'b0
endmodule
